# Fritzing sketch T6713_Arduino_I2C (saved by Fritzing 0.9.1b)
breadboards: 1

parts:
  JP1 = Header 6 [package=molex-1x6-ra]
  Part1 = Arduino Uno (Rev3)
  R1 = Resistor [tolerance=±5% resistance=4.7k package=THT]

nets:
  N1: JP1.1, Part1.A4/SDA, R1.Pin_1
  N2: JP1.2, Part1.A5/SCL
  N3: JP1.3, Part1.5V, R1.Pin_0
  N4: JP1.4, Part1.GND

notes:
  T6713
